# Fritzing sketch Wireup (saved by Fritzing 0.9.3b)
breadboards: 1
stripboards: 1

parts:
  U1 = NodeMCU V3.0
  J1 = male pin header, 4 pins [form="♂ (male)"]
  J2 = male pin header, 3 pins [form="♂ (male)"]
  M2 = Niren can bus module [package=THT]
  J3 = male pin header, 1 pin [form="♂ (male)"]
  J4 = male pin header, 1 pin [form="♂ (male)"]
  J5 = male pin header, 1 pin [form="♂ (male)"]
  J6 = male pin header, 1 pin [form="♂ (male)"]
  J7 = male pin header, 1 pin [form="♂ (male)"]
  J8 = male pin header, 1 pin [form="♂ (male)"]
  J9 = male pin header, 1 pin [form="♂ (male)"]
  VCC1 = 4 x AAA Battery Mount

nets:
  N1: U1.D4, M2.pin7
  N2: U1.GND#6, U1.GND#13, U1.GND#16, U1.GND#33, J1.pin1, M2.pin2, J3.pin1, VCC1.-
  N3: U1.D5, M2.pin6
  N4: U1.D6, M2.pin4
  N5: U1.D7, M2.pin5
  N6: U1.Vin, M2.pin1
  N7: U1.S3, M2.pin3
  N8: J1.pin2, M2.pin11, M2.pin13, J4.pin1
  N9: J1.pin3, M2.pin10, M2.pin12, J5.pin1
  N10: J1.pin4, J6.pin1
  N11: J2.pin1, J9.pin1
  N12: J2.pin2, J7.pin1
  N13: J2.pin3, J8.pin1

notes:
  10V VCC
  GND
  CAN H
  CAN L

custom parts:
  NodeMCU V3.0: ESP8266 based NodeMCU
  Niren can bus module: Niren can bus module availabe on ebay and others. No pcb view as no mechanical drawng and it wouldn't mount anyway.
